# Fritzing sketch toilet-project-display (saved by Fritzing 0.9.3b)
breadboards: 1

parts:
  U1 = NodeMCU V1.0
  R3 = Resistor [tolerance=±5% resistance=220 package=THT]
  LED1 = smd LED [color="Red (633nm)" package="1206 [SMD]"]
  LED2 = smd LED [color="Green (555nm)" package="1206 [SMD]"]
  LED3 = smd LED [color="Yellow (595nm)" package="1206 [SMD]"]
  R4 = Resistor [tolerance=±5% resistance=220 package=THT]
  R5 = Resistor [tolerance=±5% resistance=220 package=THT]

nets:
  N1: U1.D1, R3.Pin_0
  N2: U1.D2, R5.Pin_0
  N3: U1.D3, R4.Pin_0
  N4: U1.GND, LED1.cathode, LED2.cathode, LED3.cathode
  N5: R3.Pin_1, LED2.anode
  N6: LED1.anode, R5.Pin_1
  N7: LED3.anode, R4.Pin_1

custom parts:
  NodeMCU V1.0: ESP8266 based NodeMCU
